# Fritzing sketch Fritzing schets (saved by Fritzing 0.9.2b)
breadboards: 1

parts:
  Onderdeel1 = Arduino Uno (Rev3)
  LED1 = LED - 5mm [color="Red (660nm)" package="5 mm [THT]"]
  LED2 = LED - 5mm [color="Yellow (595nm)" package="5 mm [THT]"]
  LED3 = LED - 5mm [color="Green (570nm)" package="5 mm [THT]"]
  LED4 = LED - 5mm [color="Red (633nm)" package="5 mm [THT]"]
  LED5 = LED - 5mm [color="Yellow (595nm)" package="5 mm [THT]"]
  LED6 = LED - 5mm [color="Green (570nm)" package="5 mm [THT]"]
  R1 = Resistor [tolerance=±5% resistance=220 package=THT]
  R2 = Resistor [tolerance=±5% resistance=220 package=THT]
  J1 = Basic Servo

nets:
  N1: Onderdeel1.A0, J1.pulse
  N2: Onderdeel1.D12/MISO, R2.Pin_0
  N3: Onderdeel1.D13/SCK, R1.Pin_0
  N4: Onderdeel1.GND, LED1.anode, LED2.anode, LED3.anode, LED4.anode, LED5.anode, LED6.anode
  N5: LED1.cathode, LED2.cathode, LED3.cathode, R1.Pin_1
  N6: LED4.cathode, LED5.cathode, LED6.cathode, R2.Pin_1
