# Fritzing sketch Fritzing schets2 (saved by Fritzing 0.9.2b)
breadboards: 1

parts:
  Onderdeel1 = Arduino Uno (Rev3)
  LED1 = LED - 5mm [color="Red (660nm)" package="5 mm [THT]"]
  LED2 = LED - 5mm [color="Yellow (595nm)" package="5 mm [THT]"]
  LED3 = LED - 5mm [color="Green (570nm)" package="5 mm [THT]"]
  LED4 = LED - 5mm [color="Red (633nm)" package="5 mm [THT]"]
  LED5 = LED - 5mm [color="Yellow (595nm)" package="5 mm [THT]"]
  LED6 = LED - 5mm [color="Green (570nm)" package="5 mm [THT]"]
  R1 = Resistor [tolerance=±5% resistance=220 package=THT]
  R2 = Resistor [tolerance=±5% resistance=220 package=THT]
  J1 = Basic Servo
  S1 = Momentary Switch [package=ksa_sealed_tac_switch]
  S2 = Momentary Switch [package=ksa_sealed_tac_switch]
  S3 = Momentary Switch [package=ksa_sealed_tac_switch]
  S4 = Momentary Switch [package=ksa_sealed_tac_switch]
  R3 = Resistor [tolerance=±5% resistance=220 package=THT]
  R4 = Resistor [tolerance=±5% resistance=220 package=THT]
  R5 = Resistor [tolerance=±5% resistance=220 package=THT]
  R6 = Resistor [tolerance=±5% resistance=220 package=THT]
  J2 = Piezo Speaker

nets (from the schematic view):
  N1: Onderdeel1.A0, J1.pulse
  N2: Onderdeel1.D8, R5.Pin_0
  N3: Onderdeel1.D9_PWM, R6.Pin_0
  N4: Onderdeel1.D10_PWM/SS, R2.Pin_0
  N5: Onderdeel1.D11_PWM/MOSI, R3.Pin_0
  N6: Onderdeel1.D12/MISO, R4.Pin_0
  N7: Onderdeel1.D13/SCK, R1.Pin_0
  N8: Onderdeel1.D0/RX, S2.1
  N9: Onderdeel1.D1/TX, S3.2
  N10: Onderdeel1.D2, S1.1
  N11: Onderdeel1.D3_PWM, S4.1
  N12: Onderdeel1.D7, J2.pin2
  5V: Onderdeel1.5V, J1.vcc, S1.3, S2.3, S3.3, S4.3
  GND: Onderdeel1.GND, LED1.anode, LED2.anode, LED3.anode, LED4.anode, J1.gnd, J2.pin1
  N13: LED1.cathode, R1.Pin_1
  N14: LED2.cathode, R4.Pin_1
  N15: LED3.cathode, R3.Pin_1
  N16: LED4.cathode, R2.Pin_1
  N17: LED5.cathode, R6.Pin_1
  N18: LED5.anode, LED6.anode
  N19: LED6.cathode, R5.Pin_1
